// Logisim project ula-2bits.circ as structural Verilog: 12 circuits, main circuit main
module main (
  input  A0,
  input  A1,
  input  B0,
  input  B1,
  input  [2:0] \Seleção ,
  output S0,
  output S1
);

  wire operacoes_1_a___b, operacoes_1_a___b_2, operacoes_1_a___b_3, operacoes_1_borrowout,
       operacoes_1_carryout, operacoes_1_negativo;

  operacoes operacoes_1 (
    .A0(A0), .A1(A1), .B0(B0), .B1(B1), .S0(S0), .S1(S1), .\Seleção (\Seleção ), .A___B(operacoes_1_a___b),
    .A___B_2(operacoes_1_a___b_2), .A___B_3(operacoes_1_a___b_3), .Negativo(operacoes_1_negativo),
    .Carryout(operacoes_1_carryout), .Borrowout(operacoes_1_borrowout));
  LED Carryout (.in(operacoes_1_carryout));
  LED Borrowout (.in(operacoes_1_borrowout));
  LED A___B (.in(operacoes_1_a___b));
  LED A___B_2 (.in(operacoes_1_a___b_2));
  LED A___B_3 (.in(operacoes_1_a___b_3));
  LED Negativo (.in(operacoes_1_negativo));

  // Notes on the sheet:
  //   Soma = 000
  //   Subtraçaõ = 001
  //   Igual = 010
  //   Menor = 011
  //   Maior = 100
  //   ULA
endmodule

module soma (
  input  Carry_in,
  input  A,
  input  B,
  output Soma,
  output Carry_out
);

  wire and_1_out, and_2_out, and_3_out, and_4_out, and_5_out, and_6_out, and_7_out, not_1_out, not_2_out,
       not_3_out, not_4_out, not_5_out, not_6_out;

  not not_1 (not_1_out, Carry_in);
  not not_2 (not_2_out, A);
  not not_3 (not_3_out, Carry_in);
  not not_4 (not_4_out, B);
  not not_5 (not_5_out, A);
  not not_6 (not_6_out, B);
  and and_1 (and_1_out, A, B);
  and and_2 (and_2_out, Carry_in, B);
  and and_3 (and_3_out, Carry_in, A);
  and and_4 (and_4_out, not_1_out, not_2_out, B);
  and and_5 (and_5_out, not_3_out, A, not_4_out);
  and and_6 (and_6_out, Carry_in, not_5_out, not_6_out);
  and and_7 (and_7_out, Carry_in, A, B);
  or or_1 (Carry_out, and_1_out, and_2_out, and_3_out);
  or or_2 (Soma, and_4_out, and_5_out, and_6_out, and_7_out);

  // Notes on the sheet:
  //   Soma
endmodule

module soma_2bits (
  input  B0,
  input  B1,
  input  A0,
  input  A1,
  output Carry_out,
  output S1,
  output S0
);

  wire soma_2_carry_out;

  soma soma_1 (.Carry_in(soma_2_carry_out), .A(A1), .B(B1), .Soma(S1), .Carry_out(Carry_out));
  soma soma_2 (.Carry_in(1'b0), .A(A0), .B(B0), .Soma(S0), .Carry_out(soma_2_carry_out));
endmodule

module subtracao (
  input  B,
  input  A,
  input  Borrow_in,
  output \Subtração ,
  output Borrow_out
);

  wire and_1_out, and_2_out, and_3_out, and_4_out, and_5_out, and_6_out, and_7_out, not_1_out, not_2_out,
       not_3_out, not_4_out, not_5_out, not_6_out, not_7_out, not_8_out;

  not not_1 (not_1_out, A);
  not not_2 (not_2_out, B);
  not not_3 (not_3_out, A);
  not not_4 (not_4_out, Borrow_in);
  not not_5 (not_5_out, B);
  not not_6 (not_6_out, Borrow_in);
  not not_7 (not_7_out, A);
  not not_8 (not_8_out, A);
  and and_1 (and_1_out, not_1_out, not_2_out, Borrow_in);
  and and_2 (and_2_out, not_3_out, B, not_4_out);
  and and_3 (and_3_out, A, not_5_out, not_6_out);
  and and_4 (and_4_out, A, B, Borrow_in);
  and and_5 (and_5_out, not_7_out, Borrow_in);
  and and_6 (and_6_out, not_8_out, B);
  and and_7 (and_7_out, B, Borrow_in);
  or or_1 (\Subtração , and_1_out, and_2_out, and_3_out, and_4_out);
  or or_2 (Borrow_out, and_5_out, and_6_out, and_7_out);

  // Notes on the sheet:
  //   Subtração
endmodule

module subtracao_2bits (
  input  B0,
  input  B1,
  input  A0,
  input  A1,
  output Borrowout,
  output S0,
  output S1
);

  wire subtracao_2_borrow_out;

  subtracao subtracao_1 (.B(B1), .A(A1), .Borrow_in(subtracao_2_borrow_out), .\Subtração (S1), .Borrow_out(Borrowout));
  subtracao subtracao_2 (.B(B0), .A(A0), .Borrow_in(1'b0), .\Subtração (S0), .Borrow_out(subtracao_2_borrow_out));

  // Notes on the sheet:
  //   Subtração-8bits
endmodule

module igual (
  input  A,
  input  B,
  output Igual
);

  wire and_1_out, and_2_out, not_1_out, not_2_out;

  not not_1 (not_1_out, A);
  not not_2 (not_2_out, B);
  and and_1 (and_1_out, not_1_out, not_2_out);
  and and_2 (and_2_out, A, B);
  or or_1 (Igual, and_1_out, and_2_out);

  // Notes on the sheet:
  //   Igual
endmodule

module igual_2bits (
  input  A0,
  input  A1,
  input  B0,
  input  B1,
  output Igual
);

  wire igual_1_igual, igual_2_igual;

  igual igual_1 (.A(A0), .B(B0), .Igual(igual_1_igual));
  igual igual_2 (.A(A1), .B(B1), .Igual(igual_2_igual));
  and and_1 (Igual, igual_1_igual, igual_2_igual);

  // Notes on the sheet:
  //   Igual-8bits
endmodule

module menor_2bits (
  input  A0,
  input  A1,
  input  B0,
  input  B1,
  output A___B
);

  wire and_1_out, and_2_out, and_3_out, and_4_out, nor_1_out, not_1_out, not_2_out, not_3_out;

  not not_1 (not_1_out, A0);
  not not_2 (not_2_out, B0);
  not not_3 (not_3_out, A1);
  and and_1 (and_1_out, not_1_out, B0);
  and and_2 (and_2_out, A0, not_2_out);
  and and_3 (and_3_out, not_3_out, B1);
  nor nor_1 (nor_1_out, and_1_out, and_2_out);
  and and_4 (and_4_out, nor_1_out, and_3_out);
  or or_1 (A___B, and_1_out, and_4_out);

  // Notes on the sheet:
  //   Menor 2 bits
  //   A < B
endmodule

module maior_2bits (
  input  A0,
  input  A1,
  input  B0,
  input  B1,
  output A___B
);

  wire and_1_out, and_2_out, and_3_out, and_4_out, nor_1_out, not_1_out, not_2_out, not_3_out;

  not not_1 (not_1_out, A0);
  not not_2 (not_2_out, B0);
  not not_3 (not_3_out, B1);
  and and_1 (and_1_out, not_1_out, B0);
  and and_2 (and_2_out, A0, not_2_out);
  and and_3 (and_3_out, A1, not_3_out);
  nor nor_1 (nor_1_out, and_1_out, and_2_out);
  and and_4 (and_4_out, nor_1_out, and_3_out);
  or or_1 (A___B, and_2_out, and_4_out);

  // Notes on the sheet:
  //   Maior 2 bits
  //   A > B
endmodule

module comparacao (
  input  A0,
  input  A1,
  input  B0,
  input  B1,
  output A___B,
  output A___B_2,
  output A___B_3,
  output Negativo
);

  Comparator #(.width(2)) comparator_1 (.a({A1, A0}), .b({B1, B0}), .gt(A___B), .eq(A___B_2), .lt(A___B_3));

  assign Negativo = A___B_3;

  // Notes on the sheet:
  //   Comparação
endmodule

module selecao (
  input  A0,
  input  A1,
  input  B0,
  input  B1,
  input  [2:0] \Seleção ,
  output Carryout,
  output Borrowout,
  output S0,
  output S1
);

  wire igual_2bits_1_igual, maior_2bits_1_a___b, menor_2bits_1_a___b;
  wire [1:0] bit_extender_1_out, bit_extender_2_out, bit_extender_3_out, soma_2bits_1_s0,
       subtracao_2bits_1_s0;

  soma_2bits soma_2bits_1 (
    .Carry_out(Carryout), .A0(A0), .A1(A1), .B0(B0), .B1(B1), .S1(soma_2bits_1_s0[1]), .S0(soma_2bits_1_s0[0]));
  subtracao_2bits subtracao_2bits_1 (
    .Borrowout(Borrowout), .A0(A0), .A1(A1), .B0(B0), .B1(B1), .S1(subtracao_2bits_1_s0[1]),
    .S0(subtracao_2bits_1_s0[0]));
  igual_2bits igual_2bits_1 (.A0(A0), .A1(A1), .B0(B0), .B1(B1), .Igual(igual_2bits_1_igual));
  menor_2bits menor_2bits_1 (.A0(A0), .A1(A1), .B0(B0), .B1(B1), .A___B(menor_2bits_1_a___b));
  maior_2bits maior_2bits_1 (.A0(A0), .A1(A1), .B0(B0), .B1(B1), .A___B(maior_2bits_1_a___b));
  assign bit_extender_1_out = {{1{1'b0}}, igual_2bits_1_igual};  // Bit_Extender bit_extender_1
  assign bit_extender_2_out = {{1{1'b0}}, menor_2bits_1_a___b};  // Bit_Extender bit_extender_2
  assign bit_extender_3_out = {{1{1'b0}}, maior_2bits_1_a___b};  // Bit_Extender bit_extender_3
  Multiplexer #(.select(3), .width(2)) multiplexer_1 (
    .in0(soma_2bits_1_s0), .in1(subtracao_2bits_1_s0), .in2(bit_extender_1_out), .in3(bit_extender_2_out),
    .in4(bit_extender_3_out), .out({S1, S0}), .sel(\Seleção ), .en(1'b1));  // open: in5, in6, in7

  // Notes on the sheet:
  //   Seleção: pull=down
  //   Seleção
  //   Soma = 000
  //   Igual = 010
  //   Menor = 011
  //   Maior = 100
  //   Subtraçaõ = 001
endmodule

module operacoes (
  input  A0,
  input  A1,
  input  [2:0] \Seleção ,
  input  B0,
  input  B1,
  output Carryout,
  output Borrowout,
  output S0,
  output S1,
  output A___B,
  output A___B_2,
  output A___B_3,
  output Negativo
);

  selecao selecao_1 (
    .A0(A0), .A1(A1), .B0(B0), .B1(B1), .\Seleção (\Seleção ), .S0(S0), .S1(S1), .Carryout(Carryout),
    .Borrowout(Borrowout));
  comparacao comparacao_1 (
    .A0(A0), .A1(A1), .B0(B0), .B1(B1), .A___B(A___B), .A___B_2(A___B_2), .A___B_3(A___B_3),
    .Negativo(Negativo));

  // Notes on the sheet:
  //   Operações
  //   Soma = 000
  //   Igual = 010
  //   Menor = 011
  //   Maior = 100
  //   Subtraçaõ = 001
endmodule
