// Logisim project ula.circ as structural Verilog: 16 circuits, main circuit Soma-8bits
module main (
  input  A0,
  input  A1,
  input  A2,
  input  A3,
  input  A4,
  input  A5,
  input  A6,
  input  A7,
  input  B0,
  input  B1,
  input  B2,
  input  B3,
  input  B4,
  input  B5,
  input  B6,
  input  B7,
  input  [2:0] \Seleção 
);

  wire hexa_7segmentos_1_a_2, hexa_7segmentos_1_b_2, hexa_7segmentos_1_c_2, hexa_7segmentos_1_d_2,
       hexa_7segmentos_1_e, hexa_7segmentos_1_f, hexa_7segmentos_1_g, hexa_7segmentos_2_a_2,
       hexa_7segmentos_2_b_2, hexa_7segmentos_2_c_2, hexa_7segmentos_2_d_2, hexa_7segmentos_2_e,
       hexa_7segmentos_2_f, hexa_7segmentos_2_g, operacoes_1_a___b, operacoes_1_a___b_2, operacoes_1_a___b_3,
       operacoes_1_borrowout, operacoes_1_carryout, operacoes_1_negativo;
  wire [7:0] operacoes_1_s0;

  Operacoes operacoes_1 (
    .B0(B0), .B1(B1), .B2(B2), .B3(B3), .B4(B4), .B5(B5), .\Seleção (\Seleção ), .B6(B6), .B7(B7), .A0(A0),
    .A1(A1), .A2(A2), .A3(A3), .A4(A4), .A5(A5), .A6(A6), .A7(A7), .Borrowout(operacoes_1_borrowout),
    .Carryout(operacoes_1_carryout), .S0(operacoes_1_s0[0]), .S1(operacoes_1_s0[1]), .S2(operacoes_1_s0[2]),
    .S3(operacoes_1_s0[3]), .S4(operacoes_1_s0[4]), .S5(operacoes_1_s0[5]), .S6(operacoes_1_s0[6]),
    .S7(operacoes_1_s0[7]), .A___B(operacoes_1_a___b), .A___B_2(operacoes_1_a___b_2),
    .A___B_3(operacoes_1_a___b_3), .Negativo(operacoes_1_negativo));
  LED Borrowout (.in(operacoes_1_borrowout));
  LED Carryout (.in(operacoes_1_carryout));
  LED A___B (.in(operacoes_1_a___b));
  LED A___B_2 (.in(operacoes_1_a___b_2));
  LED A___B_3 (.in(operacoes_1_a___b_3));
  LED Negativo (.in(operacoes_1_negativo));
  Hexa_7segmentos hexa_7segmentos_1 (
    .a(operacoes_1_s0[0]), .b(operacoes_1_s0[1]), .c(operacoes_1_s0[2]), .d(operacoes_1_s0[3]),
    .a_2(hexa_7segmentos_1_a_2), .b_2(hexa_7segmentos_1_b_2), .c_2(hexa_7segmentos_1_c_2),
    .d_2(hexa_7segmentos_1_d_2), .e(hexa_7segmentos_1_e), .f(hexa_7segmentos_1_f), .g(hexa_7segmentos_1_g));
  _7_Segment_Display u_7_segment_display_1 (
    .g(hexa_7segmentos_1_g), .f(hexa_7segmentos_1_f), .a(hexa_7segmentos_1_a_2), .b(hexa_7segmentos_1_b_2),
    .e(hexa_7segmentos_1_e), .d(hexa_7segmentos_1_d_2), .c(hexa_7segmentos_1_c_2));  // open: dp
  Hexa_7segmentos hexa_7segmentos_2 (
    .a(operacoes_1_s0[4]), .b(operacoes_1_s0[5]), .c(operacoes_1_s0[6]), .d(operacoes_1_s0[7]),
    .a_2(hexa_7segmentos_2_a_2), .b_2(hexa_7segmentos_2_b_2), .c_2(hexa_7segmentos_2_c_2),
    .d_2(hexa_7segmentos_2_d_2), .e(hexa_7segmentos_2_e), .f(hexa_7segmentos_2_f), .g(hexa_7segmentos_2_g));
  _7_Segment_Display u_7_segment_display_2 (
    .g(hexa_7segmentos_2_g), .f(hexa_7segmentos_2_f), .a(hexa_7segmentos_2_a_2), .b(hexa_7segmentos_2_b_2),
    .e(hexa_7segmentos_2_e), .d(hexa_7segmentos_2_d_2), .c(hexa_7segmentos_2_c_2));  // open: dp

  // Notes on the sheet:
  //   Subtração = A-B
  //   Maior = A>B
  //   Menor = A<B
  //   Soma = 000
  //   Subtraçaõ = 001
  //   Igual = 010
  //   OR = 011
  //   AND = 100
  //   Maior = 101
  //   Menor = 110
endmodule

module Soma_8bits (
  input  B7,
  input  B6,
  input  B5,
  input  B4,
  input  B3,
  input  B2,
  input  B1,
  input  B0,
  input  A7,
  input  A6,
  input  A5,
  input  A4,
  input  A3,
  input  A2,
  input  A1,
  input  A0,
  output Carryout,
  output S7,
  output S6,
  output S5,
  output S4,
  output S3,
  output S2,
  output S1,
  output S0
);

  wire soma_2_carry_out, soma_3_carry_out, soma_4_carry_out, soma_5_carry_out, soma_6_carry_out,
       soma_7_carry_out, soma_8_carry_out;

  Soma soma_1 (.Carry_in(soma_3_carry_out), .A(A7), .B(B7), .Soma(S7), .Carry_out(Carryout));
  Soma soma_2 (.Carry_in(soma_4_carry_out), .A(A5), .B(B5), .Soma(S5), .Carry_out(soma_2_carry_out));
  Soma soma_3 (.Carry_in(soma_2_carry_out), .A(A6), .B(B6), .Soma(S6), .Carry_out(soma_3_carry_out));
  Soma soma_4 (.Carry_in(soma_5_carry_out), .A(A4), .B(B4), .Soma(S4), .Carry_out(soma_4_carry_out));
  Soma soma_5 (.Carry_in(soma_6_carry_out), .A(A3), .B(B3), .Soma(S3), .Carry_out(soma_5_carry_out));
  Soma soma_6 (.Carry_in(soma_8_carry_out), .A(A2), .B(B2), .Soma(S2), .Carry_out(soma_6_carry_out));
  Soma soma_7 (.Carry_in(1'b0), .A(A0), .B(B0), .Soma(S0), .Carry_out(soma_7_carry_out));
  Soma soma_8 (.Carry_in(soma_7_carry_out), .A(A1), .B(B1), .Soma(S1), .Carry_out(soma_8_carry_out));

  // Notes on the sheet:
  //   B
  //   Soma-8bits
  //   A
endmodule

module Soma (
  input  Carry_in,
  input  A,
  input  B,
  output Soma,
  output Carry_out
);

  wire and_1_out, and_2_out, and_3_out, and_4_out, and_5_out, and_6_out, and_7_out, not_1_out, not_2_out,
       not_3_out, not_4_out, not_5_out, not_6_out;

  not not_1 (not_1_out, Carry_in);
  not not_2 (not_2_out, A);
  not not_3 (not_3_out, Carry_in);
  not not_4 (not_4_out, B);
  not not_5 (not_5_out, A);
  not not_6 (not_6_out, B);
  and and_1 (and_1_out, A, B);
  and and_2 (and_2_out, Carry_in, B);
  and and_3 (and_3_out, Carry_in, A);
  and and_4 (and_4_out, not_1_out, not_2_out, B);
  and and_5 (and_5_out, not_3_out, A, not_4_out);
  and and_6 (and_6_out, Carry_in, not_5_out, not_6_out);
  and and_7 (and_7_out, Carry_in, A, B);
  or or_1 (Carry_out, and_1_out, and_2_out, and_3_out);
  or or_2 (Soma, and_4_out, and_5_out, and_6_out, and_7_out);

  // Notes on the sheet:
  //   Soma
endmodule

module Subtracao (
  input  B,
  input  A,
  input  Borrowin,
  output \Subtração ,
  output Borrowout
);

  wire and_1_out, and_2_out, and_3_out, and_4_out, and_5_out, and_6_out, and_7_out, not_1_out, not_2_out,
       not_3_out, not_4_out, not_5_out, not_6_out, not_7_out, not_8_out;

  not not_1 (not_1_out, A);
  not not_2 (not_2_out, B);
  not not_3 (not_3_out, A);
  not not_4 (not_4_out, Borrowin);
  not not_5 (not_5_out, B);
  not not_6 (not_6_out, Borrowin);
  not not_7 (not_7_out, A);
  not not_8 (not_8_out, A);
  and and_1 (and_1_out, not_1_out, not_2_out, Borrowin);
  and and_2 (and_2_out, not_3_out, B, not_4_out);
  and and_3 (and_3_out, A, not_5_out, not_6_out);
  and and_4 (and_4_out, A, B, Borrowin);
  and and_5 (and_5_out, not_7_out, Borrowin);
  and and_6 (and_6_out, not_8_out, B);
  and and_7 (and_7_out, B, Borrowin);
  or or_1 (\Subtração , and_1_out, and_2_out, and_3_out, and_4_out);
  or or_2 (Borrowout, and_5_out, and_6_out, and_7_out);
endmodule

module Subtracao_8bit (
  input  A7,
  input  A6,
  input  A5,
  input  A4,
  input  A3,
  input  A2,
  input  A1,
  input  A0,
  input  B7,
  input  B6,
  input  B5,
  input  B4,
  input  B3,
  input  B2,
  input  B1,
  input  B0,
  output Borrowout,
  output S7,
  output S6,
  output S5,
  output S4,
  output S3,
  output S2,
  output S1,
  output S0
);

  wire subtracao_1_borrowout, subtracao_3_borrowout, subtracao_4_borrowout, subtracao_5_borrowout,
       subtracao_6_borrowout, subtracao_7_borrowout, subtracao_8_borrowout;

  Subtracao subtracao_1 (
    .B(B6), .A(A6), .Borrowin(subtracao_3_borrowout), .\Subtração (S6), .Borrowout(subtracao_1_borrowout));
  Subtracao subtracao_2 (.B(B7), .A(A7), .Borrowin(subtracao_1_borrowout), .\Subtração (S7), .Borrowout(Borrowout));
  Subtracao subtracao_3 (
    .B(B5), .A(A5), .Borrowin(subtracao_4_borrowout), .\Subtração (S5), .Borrowout(subtracao_3_borrowout));
  Subtracao subtracao_4 (
    .B(B4), .A(A4), .Borrowin(subtracao_5_borrowout), .\Subtração (S4), .Borrowout(subtracao_4_borrowout));
  Subtracao subtracao_5 (
    .B(B3), .A(A3), .Borrowin(subtracao_6_borrowout), .\Subtração (S3), .Borrowout(subtracao_5_borrowout));
  Subtracao subtracao_6 (
    .B(B2), .A(A2), .Borrowin(subtracao_7_borrowout), .\Subtração (S2), .Borrowout(subtracao_6_borrowout));
  Subtracao subtracao_7 (
    .B(B1), .A(A1), .Borrowin(subtracao_8_borrowout), .\Subtração (S1), .Borrowout(subtracao_7_borrowout));
  Subtracao subtracao_8 (.B(B0), .A(A0), .Borrowin(1'b0), .\Subtração (S0), .Borrowout(subtracao_8_borrowout));

  // Notes on the sheet:
  //   B
endmodule

module OR (
  input  A0,
  input  A1,
  input  A2,
  input  A3,
  input  A4,
  input  A5,
  input  A6,
  input  A7,
  input  B0,
  input  B1,
  input  B2,
  input  B3,
  input  B4,
  input  B5,
  input  B6,
  input  B7,
  output OR
);

  or or_1 (OR, A0, A1, A2, A3, A4, A5, A6, A7, B0, B1, B2, B3, B4, B5, B6, B7);

  // Notes on the sheet:
  //   Circuito OR
endmodule

module AND (
  input  A0,
  input  A1,
  input  A2,
  input  A3,
  input  A4,
  input  A5,
  input  A6,
  input  A7,
  input  B0,
  input  B1,
  input  B2,
  input  B3,
  input  B4,
  input  B5,
  input  B6,
  input  B7,
  output AND
);

  and and_1 (AND, A0, A1, A2, A3, A4, A5, A6, A7, B0, B1, B2, B3, B4, B5, B6, B7);

  // Notes on the sheet:
  //   Circuito AND
endmodule

module Maior_8bit (
  input  A0,
  input  A1,
  input  A2,
  input  A3,
  input  A4,
  input  A5,
  input  A6,
  input  A7,
  input  B0,
  input  B1,
  input  B2,
  input  B3,
  input  B4,
  input  B5,
  input  B6,
  input  B7,
  output A___B
);

  wire and_1_out, and_2_out, and_3_out, and_4_out, and_5_out, and_6_out, and_7_out, and_8_out, and_9_out,
       and_10_out, and_11_out, and_12_out, and_13_out, and_14_out, and_15_out, and_16_out, and_18_out,
       and_19_out, and_20_out, and_21_out, and_22_out, and_23_out, and_24_out, nor_1_out, nor_2_out,
       nor_3_out, nor_4_out, nor_5_out, nor_6_out, nor_7_out, nor_8_out, not_1_out, not_2_out, not_3_out,
       not_4_out, not_5_out, not_6_out, not_7_out, not_8_out, not_9_out, not_10_out, not_11_out, not_12_out,
       not_13_out, not_14_out, not_15_out, not_16_out;

  not not_1 (not_1_out, A0);
  not not_2 (not_2_out, B0);
  not not_3 (not_3_out, A1);
  not not_4 (not_4_out, B1);
  not not_5 (not_5_out, A2);
  not not_6 (not_6_out, B2);
  not not_7 (not_7_out, A3);
  not not_8 (not_8_out, B3);
  not not_9 (not_9_out, A4);
  not not_10 (not_10_out, B4);
  not not_11 (not_11_out, A5);
  not not_12 (not_12_out, B5);
  not not_13 (not_13_out, A6);
  not not_14 (not_14_out, B6);
  not not_15 (not_15_out, A7);
  not not_16 (not_16_out, B7);
  and and_1 (and_1_out, not_1_out, B0);
  and and_2 (and_2_out, A0, not_2_out);
  and and_3 (and_3_out, not_3_out, B1);
  and and_4 (and_4_out, A1, not_4_out);
  and and_5 (and_5_out, not_5_out, B2);
  and and_6 (and_6_out, A2, not_6_out);
  and and_7 (and_7_out, not_7_out, B3);
  and and_8 (and_8_out, A3, not_8_out);
  and and_9 (and_9_out, not_9_out, B4);
  and and_10 (and_10_out, A4, not_10_out);
  and and_11 (and_11_out, not_11_out, B5);
  and and_12 (and_12_out, A5, not_12_out);
  and and_13 (and_13_out, not_13_out, B6);
  and and_14 (and_14_out, A6, not_14_out);
  and and_15 (and_15_out, not_15_out, B7);
  and and_16 (and_16_out, A7, not_16_out);
  nor nor_1 (nor_1_out, and_1_out, and_2_out);
  nor nor_2 (nor_2_out, and_3_out, and_4_out);
  nor nor_3 (nor_3_out, and_5_out, and_6_out);
  nor nor_4 (nor_4_out, and_7_out, and_8_out);
  nor nor_5 (nor_5_out, and_9_out, and_10_out);
  nor nor_6 (nor_6_out, and_11_out, and_12_out);
  nor nor_7 (nor_7_out, and_13_out, and_14_out);
  nor nor_8 (nor_8_out, and_15_out, and_16_out);
  // AND_Gate and_17 has open pins: in0=nor_1_out, in1=and_3_out, out=open
  and and_18 (and_18_out, nor_1_out, and_4_out);
  and and_19 (and_19_out, nor_1_out, nor_2_out, and_6_out);
  and and_20 (and_20_out, nor_1_out, nor_2_out, nor_3_out, and_8_out);
  and and_21 (and_21_out, nor_1_out, nor_2_out, nor_3_out, nor_4_out, and_10_out);
  and and_22 (and_22_out, nor_1_out, nor_2_out, nor_3_out, nor_4_out, nor_5_out, and_12_out);
  and and_23 (and_23_out, nor_1_out, nor_2_out, nor_3_out, nor_4_out, nor_5_out, nor_6_out, and_14_out);
  and and_24 (and_24_out, nor_1_out, nor_2_out, nor_3_out, nor_4_out, nor_6_out, nor_7_out, nor_8_out, and_16_out);
  or or_1 (A___B, and_18_out, and_2_out, and_19_out, and_20_out, and_21_out, and_22_out, and_23_out, and_24_out);

  // Notes on the sheet:
  //   Maior-8bit
  //   A maior que B
endmodule

module Igual (
  input  A,
  input  B,
  output Igual
);

  wire and_1_out, and_2_out, not_1_out, not_2_out;

  not not_1 (not_1_out, A);
  not not_2 (not_2_out, B);
  and and_1 (and_1_out, not_1_out, not_2_out);
  and and_2 (and_2_out, A, B);
  or or_1 (Igual, and_1_out, and_2_out);

  // Notes on the sheet:
  //   Igual
endmodule

module Igual_8bit (
  input  A0,
  input  A1,
  input  A2,
  input  A3,
  input  A4,
  input  A5,
  input  A6,
  input  A7,
  input  B0,
  input  B1,
  input  B2,
  input  B3,
  input  B4,
  input  B5,
  input  B6,
  input  B7,
  output Igual
);

  wire igual_1_igual, igual_2_igual, igual_3_igual, igual_4_igual, igual_5_igual, igual_6_igual,
       igual_7_igual, igual_8_igual;

  Igual igual_1 (.A(A0), .B(B0), .Igual(igual_1_igual));
  Igual igual_2 (.A(A1), .B(B1), .Igual(igual_2_igual));
  Igual igual_3 (.A(A2), .B(B2), .Igual(igual_3_igual));
  Igual igual_4 (.A(A3), .B(B3), .Igual(igual_4_igual));
  Igual igual_5 (.A(A4), .B(B4), .Igual(igual_5_igual));
  Igual igual_6 (.A(A5), .B(B5), .Igual(igual_6_igual));
  Igual igual_7 (.A(A6), .B(B6), .Igual(igual_7_igual));
  Igual igual_8 (.A(A7), .B(B7), .Igual(igual_8_igual));
  and and_1 (Igual, igual_1_igual, igual_2_igual, igual_3_igual, igual_4_igual, igual_5_igual, igual_6_igual, igual_7_igual, igual_8_igual);

  // Notes on the sheet:
  //   Igual 8-bit
endmodule

module Menor_8bit (
  input  A0,
  input  A1,
  input  A2,
  input  A3,
  input  A4,
  input  A5,
  input  A6,
  input  A7,
  input  B0,
  input  B1,
  input  B2,
  input  B3,
  input  B4,
  input  B5,
  input  B6,
  input  B7,
  output A___B
);

  wire and_1_out, and_2_out, and_3_out, and_4_out, and_5_out, and_6_out, and_7_out, and_8_out, and_9_out,
       and_10_out, and_11_out, and_12_out, and_13_out, and_14_out, and_15_out, and_16_out, and_17_out,
       and_18_out, and_19_out, and_20_out, and_21_out, and_22_out, and_23_out, nor_1_out, nor_2_out,
       nor_3_out, nor_4_out, nor_5_out, nor_6_out, nor_7_out, not_1_out, not_2_out, not_3_out, not_4_out,
       not_5_out, not_6_out, not_7_out, not_8_out, not_9_out, not_10_out, not_11_out, not_12_out, not_13_out,
       not_14_out, not_15_out, not_16_out;

  not not_1 (not_1_out, A0);
  not not_2 (not_2_out, B0);
  not not_3 (not_3_out, A1);
  not not_4 (not_4_out, B1);
  not not_5 (not_5_out, A2);
  not not_6 (not_6_out, B2);
  not not_7 (not_7_out, A3);
  not not_8 (not_8_out, B3);
  not not_9 (not_9_out, A4);
  not not_10 (not_10_out, B4);
  not not_11 (not_11_out, A5);
  not not_12 (not_12_out, B5);
  not not_13 (not_13_out, A6);
  not not_14 (not_14_out, B6);
  not not_15 (not_15_out, A7);
  not not_16 (not_16_out, B7);
  and and_1 (and_1_out, not_1_out, B0);
  and and_2 (and_2_out, A0, not_2_out);
  and and_3 (and_3_out, not_3_out, B1);
  and and_4 (and_4_out, A1, not_4_out);
  and and_5 (and_5_out, not_5_out, B2);
  and and_6 (and_6_out, A2, not_6_out);
  and and_7 (and_7_out, not_7_out, B3);
  and and_8 (and_8_out, A3, not_8_out);
  and and_9 (and_9_out, not_9_out, B4);
  and and_10 (and_10_out, A4, not_10_out);
  and and_11 (and_11_out, not_11_out, B5);
  and and_12 (and_12_out, A5, not_12_out);
  and and_13 (and_13_out, not_13_out, B6);
  and and_14 (and_14_out, A6, not_14_out);
  and and_15 (and_15_out, not_15_out, B7);
  and and_16 (and_16_out, A7, not_16_out);
  nor nor_1 (nor_1_out, and_1_out, and_2_out);
  nor nor_2 (nor_2_out, and_3_out, and_4_out);
  nor nor_3 (nor_3_out, and_5_out, and_6_out);
  nor nor_4 (nor_4_out, and_7_out, and_8_out);
  nor nor_5 (nor_5_out, and_9_out, and_10_out);
  nor nor_6 (nor_6_out, and_11_out, and_12_out);
  nor nor_7 (nor_7_out, and_13_out, and_14_out);
  // NOR_Gate nor_8 has open pins: in0=and_15_out, in1=and_16_out, out=open
  and and_17 (and_17_out, nor_1_out, and_3_out);
  and and_18 (and_18_out, nor_1_out, and_5_out, nor_2_out);
  and and_19 (and_19_out, nor_1_out, nor_2_out, nor_3_out, and_7_out);
  and and_20 (and_20_out, nor_1_out, nor_2_out, nor_3_out, nor_4_out, and_9_out);
  and and_21 (and_21_out, nor_1_out, nor_2_out, nor_3_out, nor_4_out, nor_5_out, and_11_out);
  and and_22 (and_22_out, nor_1_out, nor_2_out, nor_3_out, nor_4_out, nor_5_out, nor_6_out, and_13_out);
  and and_23 (and_23_out, nor_1_out, nor_2_out, nor_3_out, nor_4_out, nor_5_out, nor_6_out, nor_7_out, and_16_out);
  or or_1 (A___B, and_1_out, and_17_out, and_18_out, and_19_out, and_20_out, and_21_out, and_22_out, and_23_out);

  // Notes on the sheet:
  //   Menor-8bit
  //   A menor que B
endmodule

module Selecao (
  input  A0,
  input  A1,
  input  A2,
  input  A3,
  input  A4,
  input  A5,
  input  A6,
  input  A7,
  input  B0,
  input  B1,
  input  B2,
  input  B3,
  input  B4,
  input  B5,
  input  B6,
  input  B7,
  input  [2:0] \Seleção ,
  output Carryout,
  output Borrowout,
  output S0,
  output S1,
  output S2,
  output S3,
  output S4,
  output S5,
  output S6,
  output S7
);

  wire and_1_and, igual_8bit_1_igual, maior_8bit_1_a___b, menor_8bit_1_a___b, or_1_or;
  wire [7:0] bit_extender_1_out, bit_extender_2_out, bit_extender_3_out, bit_extender_4_out,
       bit_extender_5_out, soma_8bits_1_s0, subtracao_8bit_1_s0;

  Soma_8bits soma_8bits_1 (
    .Carryout(Carryout), .B7(B7), .B6(B6), .B5(B5), .B4(B4), .B3(B3), .B2(B2), .B1(B1), .B0(B0), .A7(A7),
    .A6(A6), .A5(A5), .A4(A4), .A3(A3), .A2(A2), .A1(A1), .A0(A0), .S7(soma_8bits_1_s0[7]),
    .S6(soma_8bits_1_s0[6]), .S5(soma_8bits_1_s0[5]), .S4(soma_8bits_1_s0[4]), .S3(soma_8bits_1_s0[3]),
    .S2(soma_8bits_1_s0[2]), .S1(soma_8bits_1_s0[1]), .S0(soma_8bits_1_s0[0]));
  Subtracao_8bit subtracao_8bit_1 (
    .Borrowout(Borrowout), .A7(A7), .A6(A6), .A5(A5), .A4(A4), .A3(A3), .A2(A2), .A1(A1), .A0(A0), .B7(B7),
    .B6(B6), .B5(B5), .B4(B4), .B3(B3), .B2(B2), .B1(B1), .B0(B0), .S7(subtracao_8bit_1_s0[7]),
    .S6(subtracao_8bit_1_s0[6]), .S5(subtracao_8bit_1_s0[5]), .S4(subtracao_8bit_1_s0[4]),
    .S3(subtracao_8bit_1_s0[3]), .S2(subtracao_8bit_1_s0[2]), .S1(subtracao_8bit_1_s0[1]),
    .S0(subtracao_8bit_1_s0[0]));
  Igual_8bit igual_8bit_1 (
    .A0(A0), .A1(A1), .A2(A2), .A3(A3), .A4(A4), .A5(A5), .A6(A6), .A7(A7), .B0(B0), .B1(B1), .B2(B2),
    .B3(B3), .B4(B4), .B5(B5), .B6(B6), .B7(B7), .Igual(igual_8bit_1_igual));
  OR or_1 (
    .A0(A0), .A1(A1), .A2(A2), .A3(A3), .A4(A4), .A5(A5), .A6(A6), .A7(A7), .B0(B0), .B1(B1), .B2(B2),
    .B3(B3), .B4(B4), .B5(B5), .B6(B6), .B7(B7), .OR(or_1_or));
  AND and_1 (
    .A0(A0), .A1(A1), .A2(A2), .A3(A3), .A4(A4), .A5(A5), .A6(A6), .A7(A7), .B0(B0), .B1(B1), .B2(B2),
    .B3(B3), .B4(B4), .B5(B5), .B6(B6), .B7(B7), .AND(and_1_and));
  Maior_8bit maior_8bit_1 (
    .A0(A0), .A1(A1), .A2(A2), .A3(A3), .A4(A4), .A5(A5), .A6(A6), .A7(A7), .B0(B0), .B1(B1), .B2(B2),
    .B3(B3), .B4(B4), .B5(B5), .B6(B6), .B7(B7), .A___B(maior_8bit_1_a___b));
  Menor_8bit menor_8bit_1 (
    .A0(A0), .A1(A1), .A2(A2), .A3(A3), .A4(A4), .A5(A5), .A6(A6), .A7(A7), .B0(B0), .B1(B1), .B2(B2),
    .B3(B3), .B4(B4), .B5(B5), .B6(B6), .B7(B7), .A___B(menor_8bit_1_a___b));
  assign bit_extender_1_out = {{7{1'b0}}, igual_8bit_1_igual};  // Bit_Extender bit_extender_1
  assign bit_extender_2_out = {{7{1'b0}}, or_1_or};  // Bit_Extender bit_extender_2
  assign bit_extender_3_out = {{7{1'b0}}, and_1_and};  // Bit_Extender bit_extender_3
  assign bit_extender_4_out = {{7{1'b0}}, maior_8bit_1_a___b};  // Bit_Extender bit_extender_4
  assign bit_extender_5_out = {{7{1'b0}}, menor_8bit_1_a___b};  // Bit_Extender bit_extender_5
  Multiplexer #(.select(3), .width(8)) multiplexer_1 (
    .in0(soma_8bits_1_s0), .in1(subtracao_8bit_1_s0), .in2(bit_extender_1_out), .in3(bit_extender_2_out),
    .in4(bit_extender_3_out), .in5(bit_extender_4_out), .in6(bit_extender_5_out),
    .out({S7, S6, S5, S4, S3, S2, S1, S0}), .sel(\Seleção ), .en(1'b1));  // open: in7

  // Notes on the sheet:
  //   Seleção: pull=down
  //   Soma = 000
  //   Igual = 010
  //   OR = 011
  //   AND = 100
  //   Maior = 101
  //   Subtraçaõ = 001
  //   Menor = 110
endmodule

module \Comparação  (
  input  A0,
  input  A1,
  input  A2,
  input  A3,
  input  A4,
  input  A5,
  input  A6,
  input  A7,
  input  B0,
  input  B1,
  input  B2,
  input  B3,
  input  B4,
  input  B5,
  input  B6,
  input  B7,
  output A___B,
  output A___B_2,
  output A___B_3,
  output Negativo
);

  Comparator comparator_1 (
    .a({A7, A6, A5, A4, A3, A2, A1, A0}), .b({B7, B6, B5, B4, B3, B2, B1, B0}), .gt(A___B), .eq(A___B_2),
    .lt(A___B_3));

  assign Negativo = A___B_3;

  // Notes on the sheet:
  //   Comparação
endmodule

module Hexa_7segmentos (
  input  a,
  input  b,
  input  c,
  input  d,
  output a_2,
  output b_2,
  output c_2,
  output d_2,
  output e,
  output f,
  output g
);

  wire and_1_out, and_2_out, and_3_out, and_4_out, and_5_out, and_6_out, and_7_out, and_8_out, and_9_out,
       and_10_out, and_11_out, and_12_out, and_13_out, and_14_out, and_15_out, and_16_out, and_17_out,
       and_18_out, and_19_out, and_20_out, and_21_out, and_22_out, and_23_out, and_24_out, and_25_out,
       and_26_out, and_27_out, and_28_out, and_29_out, and_30_out, and_31_out, and_32_out, and_33_out,
       and_34_out, and_35_out, and_36_out, not_1_out, not_2_out, not_3_out, not_4_out, not_5_out, not_6_out,
       not_7_out, not_8_out, not_9_out, not_10_out, not_11_out, not_12_out, not_13_out, not_14_out,
       not_15_out, not_16_out, not_17_out, not_18_out, not_19_out, not_20_out, not_21_out, not_22_out,
       not_23_out, not_24_out, not_25_out, not_26_out, not_27_out, not_28_out, not_29_out, not_30_out,
       not_31_out, not_32_out, not_33_out, not_34_out, not_35_out, not_36_out, not_37_out, not_38_out,
       not_39_out, not_40_out, not_41_out, not_42_out, not_43_out, not_44_out, not_45_out, not_46_out,
       or_1_out, or_2_out, or_3_out, or_4_out, or_5_out, or_6_out, or_7_out, or_8_out, or_10_out, or_11_out,
       or_12_out, or_13_out;

  not not_1 (not_1_out, a);
  not not_2 (not_2_out, d);
  not not_3 (not_3_out, b);
  not not_4 (not_4_out, d);
  not not_5 (not_5_out, a);
  not not_6 (not_6_out, b);
  not not_7 (not_7_out, c);
  not not_8 (not_8_out, b);
  not not_9 (not_9_out, d);
  not not_10 (not_10_out, b);
  not not_11 (not_11_out, c);
  not not_12 (not_12_out, a);
  not not_13 (not_13_out, a);
  not not_14 (not_14_out, c);
  not not_15 (not_15_out, d);
  not not_16 (not_16_out, c);
  not not_17 (not_17_out, c);
  not not_18 (not_18_out, a);
  not not_19 (not_19_out, b);
  not not_20 (not_20_out, a);
  not not_21 (not_21_out, b);
  not not_22 (not_22_out, c);
  not not_23 (not_23_out, a);
  not not_24 (not_24_out, d);
  not not_25 (not_25_out, a);
  not not_26 (not_26_out, b);
  not not_27 (not_27_out, b);
  not not_28 (not_28_out, c);
  not not_29 (not_29_out, d);
  not not_30 (not_30_out, b);
  not not_31 (not_31_out, c);
  not not_32 (not_32_out, d);
  not not_33 (not_33_out, d);
  not not_34 (not_34_out, b);
  not not_35 (not_35_out, d);
  not not_36 (not_36_out, b);
  not not_37 (not_37_out, d);
  not not_38 (not_38_out, c);
  not not_39 (not_39_out, d);
  not not_40 (not_40_out, a);
  not not_41 (not_41_out, c);
  not not_42 (not_42_out, b);
  not not_43 (not_43_out, b);
  not not_44 (not_44_out, c);
  not not_45 (not_45_out, a);
  not not_46 (not_46_out, d);
  and and_1 (and_1_out, b, c);
  and and_2 (and_2_out, not_1_out, c);
  and and_3 (and_3_out, a, not_2_out);
  and and_4 (and_4_out, not_3_out, not_4_out);
  and and_5 (and_5_out, not_5_out, b, d);
  and and_6 (and_6_out, a, not_6_out, not_7_out);
  and and_7 (and_7_out, not_8_out, not_9_out);
  and and_8 (and_8_out, not_10_out, not_11_out);
  and and_9 (and_9_out, not_12_out, c, d);
  and and_10 (and_10_out, not_13_out, not_14_out, not_15_out);
  and and_11 (and_11_out, a, not_16_out, d);
  and and_12 (and_12_out, not_17_out, d);
  and and_13 (and_13_out, not_18_out, d);
  and and_14 (and_14_out, a, not_19_out);
  and and_15 (and_15_out, not_20_out, b);
  and and_16 (and_16_out, not_21_out, not_22_out);
  and and_17 (and_17_out, not_23_out, c, not_24_out);
  and and_18 (and_18_out, not_25_out, not_26_out, c);
  and and_19 (and_19_out, a, not_27_out, d);
  and and_20 (and_20_out, b, not_28_out, d);
  and and_21 (and_21_out, a, b, not_29_out);
  and and_22 (and_22_out, not_30_out, not_31_out, not_32_out);
  and and_23 (and_23_out, c, not_33_out);
  and and_24 (and_24_out, a, c);
  and and_25 (and_25_out, a, b);
  and and_26 (and_26_out, not_34_out, not_35_out);
  and and_27 (and_27_out, a, c);
  and and_28 (and_28_out, a, not_36_out);
  and and_29 (and_29_out, b, not_37_out);
  and and_30 (and_30_out, not_38_out, not_39_out);
  and and_31 (and_31_out, not_40_out, b, not_41_out);
  and and_32 (and_32_out, a, c);
  and and_33 (and_33_out, not_42_out, c);
  and and_34 (and_34_out, a, not_43_out);
  and and_35 (and_35_out, b, not_44_out, d);
  and and_36 (and_36_out, not_45_out, b, not_46_out);
  or or_1 (or_1_out, and_1_out, and_2_out, and_3_out);
  or or_2 (or_2_out, and_4_out, and_5_out, and_6_out);
  or or_3 (or_3_out, and_7_out, and_8_out);
  or or_4 (or_4_out, and_9_out, and_10_out, and_11_out);
  or or_5 (or_5_out, and_12_out, and_13_out);
  or or_6 (or_6_out, and_14_out, and_15_out, and_16_out);
  or or_7 (or_7_out, and_17_out, and_18_out, and_19_out);
  or or_8 (or_8_out, and_20_out, and_21_out, and_22_out);
  or or_9 (e, and_23_out, and_24_out, and_25_out, and_26_out);
  or or_10 (or_10_out, and_27_out, and_28_out, and_29_out);
  or or_11 (or_11_out, and_30_out, and_31_out);
  or or_12 (or_12_out, and_32_out, and_33_out);
  or or_13 (or_13_out, and_34_out, and_35_out, and_36_out);
  or or_14 (a_2, or_1_out, or_2_out);
  or or_15 (b_2, or_3_out, or_4_out);
  or or_16 (c_2, or_5_out, or_6_out);
  or or_17 (d_2, or_7_out, or_8_out);
  or or_18 (f, or_10_out, or_11_out);
  or or_19 (g, or_12_out, or_13_out);
endmodule

module Operacoes (
  input  A0,
  input  A1,
  input  A2,
  input  A3,
  input  A4,
  input  A5,
  input  A6,
  input  A7,
  input  B0,
  input  B1,
  input  B2,
  input  B3,
  input  B4,
  input  B5,
  input  [2:0] \Seleção ,
  input  B6,
  input  B7,
  output Borrowout,
  output Carryout,
  output S0,
  output S1,
  output S2,
  output S3,
  output S4,
  output S5,
  output S6,
  output S7,
  output A___B,
  output A___B_2,
  output A___B_3,
  output Negativo
);

  Selecao selecao_1 (
    .A0(A0), .A1(A1), .A2(A2), .A3(A3), .A4(A4), .A5(A5), .A6(A6), .A7(A7), .B0(B0), .B1(B1), .B2(B2),
    .B3(B3), .B4(B4), .B5(B5), .B6(B6), .B7(B7), .\Seleção (\Seleção ), .Borrowout(Carryout),
    .Carryout(Borrowout), .S0(S0), .S1(S1), .S2(S2), .S3(S3), .S4(S4), .S5(S5), .S6(S6), .S7(S7));
  \Comparação  \comparação_1  (
    .A0(A0), .A1(A1), .A2(A2), .A3(A3), .A4(A4), .A5(A5), .A6(A6), .A7(A7), .B0(B0), .B1(B1), .B2(B2),
    .B3(B3), .B4(B4), .B5(B5), .B6(B6), .B7(B7), .A___B(A___B), .A___B_2(A___B_2), .A___B_3(A___B_3),
    .Negativo(Negativo));
endmodule

module Decimal_7segmentos (
  input  in_1,
  input  in_2,
  input  in_3,
  input  in_4,
  input  in_5,
  input  in_6,
  input  in_7,
  input  in_8,
  input  in_9,
  input  in_10
);

  wire or_1_out, or_2_out, or_3_out, or_4_out, or_5_out, or_6_out, or_7_out;

  or or_1 (or_1_out, in_1, in_3, in_4, in_6, in_7, in_8, in_9, in_10);
  or or_2 (or_2_out, in_1, in_2, in_3, in_4, in_5, in_8, in_9, in_10);
  or or_3 (or_3_out, in_1, in_2, in_10, in_9, in_8, in_7, in_6, in_5, in_4);
  or or_4 (or_4_out, in_1, in_3, in_4, in_6, in_7, in_9, in_10);
  or or_5 (or_5_out, in_1, in_3, in_7, in_9);
  or or_6 (or_6_out, in_1, in_5, in_6, in_7, in_9, in_10);
  or or_7 (or_7_out, in_3, in_4, in_5, in_6, in_7, in_9, in_10);
  _7_Segment_Display u_7_segment_display_1 (
    .g(or_7_out), .f(or_6_out), .a(or_1_out), .b(or_2_out), .e(or_5_out), .d(or_4_out), .c(or_3_out));  // open: dp
endmodule
