// Logisim project TrabalhoULA.circ as structural Verilog
module Soma (
  input  Carryin,
  input  A,
  input  B,
  output Soma,
  output Carryout
);

  wire and_1_out, and_2_out, and_3_out, and_4_out, and_5_out, and_6_out, and_7_out, not_1_out, not_2_out,
       not_3_out, not_4_out, not_5_out, not_6_out;

  not not_1 (not_1_out, Carryin);
  not not_2 (not_2_out, A);
  not not_3 (not_3_out, Carryin);
  not not_4 (not_4_out, B);
  not not_5 (not_5_out, A);
  not not_6 (not_6_out, B);
  and and_1 (and_1_out, A, B);
  and and_2 (and_2_out, Carryin, B);
  and and_3 (and_3_out, Carryin, A);
  and and_4 (and_4_out, not_1_out, not_2_out, B);
  and and_5 (and_5_out, not_3_out, A, not_4_out);
  and and_6 (and_6_out, Carryin, not_5_out, not_6_out);
  and and_7 (and_7_out, Carryin, A, B);
  or or_1 (Carryout, and_1_out, and_2_out, and_3_out);
  or or_2 (Soma, and_4_out, and_5_out, and_6_out, and_7_out);
endmodule

module Soma_8bit (
  input  B7,
  input  B6,
  input  B5,
  input  B4,
  input  B3,
  input  B2,
  input  B1,
  input  B0,
  input  A7,
  input  A6,
  input  A5,
  input  A4,
  input  A3,
  input  A2,
  input  A1,
  input  A0,
  output Carry_out,
  output out_18,
  output out_19,
  output out_20,
  output out_21,
  output out_22,
  output out_23,
  output out_24,
  output out_25
);

  wire soma_1_carryout, soma_3_carryout, soma_4_carryout, soma_5_carryout, soma_6_carryout, soma_7_carryout,
       soma_8_carryout, undriven, undriven_2, undriven_3, undriven_4, undriven_5, undriven_6, undriven_7,
       undriven_8, undriven_9, undriven_10, undriven_11, undriven_12, undriven_13, undriven_14, undriven_15,
       undriven_16;

  Soma soma_1 (.Carryin(soma_3_carryout), .A(undriven_12), .B(undriven_2), .Soma(out_19), .Carryout(soma_1_carryout));
  Soma soma_2 (.Carryin(soma_1_carryout), .A(undriven_8), .B(undriven), .Soma(out_18), .Carryout(Carry_out));
  Soma soma_3 (.Carryin(soma_4_carryout), .A(undriven_13), .B(undriven_3), .Soma(out_20), .Carryout(soma_3_carryout));
  Soma soma_4 (.Carryin(soma_5_carryout), .A(undriven_10), .B(undriven_4), .Soma(out_21), .Carryout(soma_4_carryout));
  Soma soma_5 (.Carryin(soma_7_carryout), .A(undriven_11), .B(undriven_5), .Soma(out_22), .Carryout(soma_5_carryout));
  Soma soma_6 (.Carryin(soma_8_carryout), .A(undriven_15), .B(undriven_7), .Soma(out_24), .Carryout(soma_6_carryout));
  Soma soma_7 (.Carryin(soma_6_carryout), .A(undriven_14), .B(undriven_6), .Soma(out_23), .Carryout(soma_7_carryout));
  Soma soma_8 (.Carryin(1'b0), .A(undriven_16), .B(undriven_9), .Soma(out_25), .Carryout(soma_8_carryout));

  // Notes on the sheet:
  //   B
  //   A
endmodule
