// Logisim project TrabalhoULA1.0.circ as structural Verilog
module Soma (
  input  Carryin,
  input  A,
  input  B,
  output Soma,
  output Carryout
);

  wire and_1_out, and_2_out, and_3_out, and_4_out, and_5_out, and_6_out, and_7_out, not_1_out, not_2_out,
       not_3_out, not_4_out, not_5_out, not_6_out;

  not not_1 (not_1_out, Carryin);
  not not_2 (not_2_out, A);
  not not_3 (not_3_out, Carryin);
  not not_4 (not_4_out, B);
  not not_5 (not_5_out, A);
  not not_6 (not_6_out, B);
  and and_1 (and_1_out, A, B);
  and and_2 (and_2_out, Carryin, B);
  and and_3 (and_3_out, Carryin, A);
  and and_4 (and_4_out, not_1_out, not_2_out, B);
  and and_5 (and_5_out, not_3_out, A, not_4_out);
  and and_6 (and_6_out, Carryin, not_5_out, not_6_out);
  and and_7 (and_7_out, Carryin, A, B);
  or or_1 (Carryout, and_1_out, and_2_out, and_3_out);
  or or_2 (Soma, and_4_out, and_5_out, and_6_out, and_7_out);
endmodule

module Soma_8bit (
  input  B7,
  input  B6,
  input  B5,
  input  B4,
  input  B3,
  input  B2,
  input  B1,
  input  B0,
  input  A7,
  input  A6,
  input  A5,
  input  A4,
  input  A3,
  input  A2,
  input  A1,
  input  A0,
  output Carry_out,
  output out_18,
  output out_19,
  output out_20,
  output out_21,
  output out_22,
  output out_23,
  output out_24,
  output out_25
);

  wire soma_1_carryout, soma_3_carryout, soma_4_carryout, soma_5_carryout, soma_6_carryout, soma_7_carryout,
       soma_8_carryout;

  Soma soma_1 (.Carryin(soma_4_carryout), .A(A6), .B(B6), .Soma(out_19), .Carryout(soma_1_carryout));
  Soma soma_2 (.Carryin(soma_1_carryout), .A(A7), .B(B7), .Soma(out_18), .Carryout(Carry_out));
  Soma soma_3 (.Carryin(soma_5_carryout), .A(A4), .B(B4), .Soma(out_21), .Carryout(soma_3_carryout));
  Soma soma_4 (.Carryin(soma_3_carryout), .A(A5), .B(B5), .Soma(out_20), .Carryout(soma_4_carryout));
  Soma soma_5 (.Carryin(soma_6_carryout), .A(A3), .B(B3), .Soma(out_22), .Carryout(soma_5_carryout));
  Soma soma_6 (.Carryin(soma_7_carryout), .A(A2), .B(B2), .Soma(out_23), .Carryout(soma_6_carryout));
  Soma soma_7 (.Carryin(soma_8_carryout), .A(A1), .B(B1), .Soma(out_24), .Carryout(soma_7_carryout));
  Soma soma_8 (.Carryin(1'b0), .A(A0), .B(B0), .Soma(out_25), .Carryout(soma_8_carryout));

  // Notes on the sheet:
  //   B
  //   A
endmodule

module Subtracao (
  input  B,
  input  A,
  input  Borrowin,
  output \Subtração ,
  output Borrowout
);

  wire and_1_out, and_2_out, and_3_out, and_4_out, and_5_out, and_6_out, and_7_out, not_1_out, not_2_out,
       not_3_out, not_4_out, not_5_out, not_6_out, not_7_out, not_8_out;

  not not_1 (not_1_out, A);
  not not_2 (not_2_out, B);
  not not_3 (not_3_out, A);
  not not_4 (not_4_out, Borrowin);
  not not_5 (not_5_out, B);
  not not_6 (not_6_out, Borrowin);
  not not_7 (not_7_out, A);
  not not_8 (not_8_out, A);
  and and_1 (and_1_out, not_1_out, not_2_out, Borrowin);
  and and_2 (and_2_out, not_3_out, B, not_4_out);
  and and_3 (and_3_out, A, not_5_out, not_6_out);
  and and_4 (and_4_out, A, B, Borrowin);
  and and_5 (and_5_out, not_7_out, Borrowin);
  and and_6 (and_6_out, not_8_out, B);
  and and_7 (and_7_out, B, Borrowin);
  or or_1 (\Subtração , and_1_out, and_2_out, and_3_out, and_4_out);
  or or_2 (Borrowout, and_5_out, and_6_out, and_7_out);
endmodule

module Subtracao_8bit (
  input  A7,
  input  A6,
  input  A5,
  input  A4,
  input  A3,
  input  A2,
  input  A1,
  input  A0,
  input  B7,
  input  B6,
  input  B5,
  input  B4,
  input  B3,
  input  B2,
  input  B1,
  input  B0,
  output out_17,
  output S7,
  output S6,
  output S5,
  output S4,
  output S3,
  output S2,
  output S1,
  output S0
);

  wire subtracao_2_borrowout, subtracao_3_borrowout, subtracao_4_borrowout, subtracao_5_borrowout,
       subtracao_6_borrowout, subtracao_7_borrowout, subtracao_8_borrowout;

  Subtracao subtracao_1 (.B(B7), .A(A7), .Borrowin(subtracao_2_borrowout), .\Subtração (S7), .Borrowout(out_17));
  Subtracao subtracao_2 (
    .B(B6), .A(A6), .Borrowin(subtracao_3_borrowout), .\Subtração (S6), .Borrowout(subtracao_2_borrowout));
  Subtracao subtracao_3 (
    .B(B5), .A(A5), .Borrowin(subtracao_4_borrowout), .\Subtração (S5), .Borrowout(subtracao_3_borrowout));
  Subtracao subtracao_4 (
    .B(B4), .A(A4), .Borrowin(subtracao_5_borrowout), .\Subtração (S4), .Borrowout(subtracao_4_borrowout));
  Subtracao subtracao_5 (
    .B(B3), .A(A3), .Borrowin(subtracao_6_borrowout), .\Subtração (S3), .Borrowout(subtracao_5_borrowout));
  Subtracao subtracao_6 (
    .B(B2), .A(A2), .Borrowin(subtracao_7_borrowout), .\Subtração (S2), .Borrowout(subtracao_6_borrowout));
  Subtracao subtracao_7 (
    .B(B1), .A(A1), .Borrowin(subtracao_8_borrowout), .\Subtração (S1), .Borrowout(subtracao_7_borrowout));
  Subtracao subtracao_8 (.B(B0), .A(A0), .Borrowin(1'b0), .\Subtração (S0), .Borrowout(subtracao_8_borrowout));

  // Notes on the sheet:
  //   A
endmodule

module \Seleção  (
  input  A0,
  input  A1,
  input  A2,
  input  A3,
  input  A4,
  input  A5,
  input  A6,
  input  A7,
  input  B0,
  input  B1,
  input  B2,
  input  B3,
  input  B4,
  input  B5,
  input  B6,
  input  B7,
  output Carryout,
  output Borrowout,
  output S0,
  output S1,
  output S2,
  output S3,
  output S4,
  output S5,
  output S6,
  output S7
);

  wire [2:0] undriven;
  wire [7:0] bit_extender_1_out, soma_8bit_1_out_25, subtracao_8bit_1_s0;

  Soma_8bit soma_8bit_1 (
    .Carry_out(Carryout), .B7(B7), .B6(B6), .B5(B5), .B4(B4), .B3(B3), .B2(B2), .B1(B1), .B0(B0), .A7(A7),
    .A6(A6), .A5(A5), .A4(A4), .A3(A3), .A2(A2), .A1(A1), .A0(A0), .out_18(soma_8bit_1_out_25[7]),
    .out_19(soma_8bit_1_out_25[6]), .out_20(soma_8bit_1_out_25[5]), .out_21(soma_8bit_1_out_25[4]),
    .out_22(soma_8bit_1_out_25[3]), .out_23(soma_8bit_1_out_25[2]), .out_24(soma_8bit_1_out_25[1]),
    .out_25(soma_8bit_1_out_25[0]));
  Subtracao_8bit subtracao_8bit_1 (
    .out_17(Borrowout), .A7(A7), .A6(A6), .A5(A5), .A4(A4), .A3(A3), .A2(A2), .A1(A1), .A0(A0), .B7(B7),
    .B6(B6), .B5(B5), .B4(B4), .B3(B3), .B2(B2), .B1(B1), .B0(B0), .S7(subtracao_8bit_1_s0[7]),
    .S6(subtracao_8bit_1_s0[6]), .S5(subtracao_8bit_1_s0[5]), .S4(subtracao_8bit_1_s0[4]),
    .S3(subtracao_8bit_1_s0[3]), .S2(subtracao_8bit_1_s0[2]), .S1(subtracao_8bit_1_s0[1]),
    .S0(subtracao_8bit_1_s0[0]));
  Bit_Extender #(.in_width(1), .out_width(8)) bit_extender_1 (.out(bit_extender_1_out));  // open: in
  Multiplexer #(.select(3), .width(8)) multiplexer_1 (
    .in0(soma_8bit_1_out_25), .in1(subtracao_8bit_1_s0), .in2(bit_extender_1_out),
    .out({S7, S6, S5, S4, S3, S2, S1, S0}), .sel(undriven), .en(1'b1));  // open: in3, in4, in5, in6, in7
endmodule
