// Logisim project TrabalhoULA2.0.circ as structural Verilog
module Soma_8bit (
  input  B7,
  input  B6,
  input  B5,
  input  B4,
  input  B3,
  input  B2,
  input  B1,
  input  B0,
  input  A7,
  input  A6,
  input  A5,
  input  A4,
  input  A3,
  input  A2,
  input  A1,
  input  A0,
  output Carry_out,
  output out_18,
  output out_19,
  output out_20,
  output out_21,
  output out_22,
  output out_23,
  output out_24,
  output out_25
);

  wire soma_1_carryout, soma_3_carryout, soma_4_carryout, soma_5_carryout, soma_6_carryout, soma_7_carryout,
       soma_8_carryout;

  Soma soma_1 (.Carryin(soma_4_carryout), .A(A6), .B(B6), .Soma(out_19), .Carryout(soma_1_carryout));
  Soma soma_2 (.Carryin(soma_1_carryout), .A(A7), .B(B7), .Soma(out_18), .Carryout(Carry_out));
  Soma soma_3 (.Carryin(soma_5_carryout), .A(A4), .B(B4), .Soma(out_21), .Carryout(soma_3_carryout));
  Soma soma_4 (.Carryin(soma_3_carryout), .A(A5), .B(B5), .Soma(out_20), .Carryout(soma_4_carryout));
  Soma soma_5 (.Carryin(soma_7_carryout), .A(A3), .B(B3), .Soma(out_22), .Carryout(soma_5_carryout));
  Soma soma_6 (.Carryin(soma_8_carryout), .A(A1), .B(B1), .Soma(out_24), .Carryout(soma_6_carryout));
  Soma soma_7 (.Carryin(soma_6_carryout), .A(A2), .B(B2), .Soma(out_23), .Carryout(soma_7_carryout));
  Soma soma_8 (.Carryin(1'b0), .A(A0), .B(B0), .Soma(out_25), .Carryout(soma_8_carryout));

  // Notes on the sheet:
  //   B
  //   A
endmodule

module Soma (
  input  Carryin,
  input  A,
  input  B,
  output Soma,
  output Carryout
);

  wire and_1_out, and_2_out, and_3_out, and_4_out, and_5_out, and_6_out, and_7_out, not_1_out, not_2_out,
       not_3_out, not_4_out, not_5_out, not_6_out;

  not not_1 (not_1_out, Carryin);
  not not_2 (not_2_out, A);
  not not_3 (not_3_out, Carryin);
  not not_4 (not_4_out, B);
  not not_5 (not_5_out, A);
  not not_6 (not_6_out, B);
  and and_1 (and_1_out, A, B);
  and and_2 (and_2_out, Carryin, B);
  and and_3 (and_3_out, Carryin, A);
  and and_4 (and_4_out, not_1_out, not_2_out, B);
  and and_5 (and_5_out, not_3_out, A, not_4_out);
  and and_6 (and_6_out, Carryin, not_5_out, not_6_out);
  and and_7 (and_7_out, Carryin, A, B);
  or or_1 (Carryout, and_1_out, and_2_out, and_3_out);
  or or_2 (Soma, and_4_out, and_5_out, and_6_out, and_7_out);
endmodule

module Subtracao (
  input  B,
  input  A,
  input  Borrowin,
  output \Subtração ,
  output Borrowout
);

  wire and_1_out, and_2_out, and_3_out, and_4_out, and_5_out, and_6_out, and_7_out, not_1_out, not_2_out,
       not_3_out, not_4_out, not_5_out, not_6_out, not_7_out, not_8_out;

  not not_1 (not_1_out, A);
  not not_2 (not_2_out, B);
  not not_3 (not_3_out, A);
  not not_4 (not_4_out, Borrowin);
  not not_5 (not_5_out, B);
  not not_6 (not_6_out, Borrowin);
  not not_7 (not_7_out, A);
  not not_8 (not_8_out, A);
  and and_1 (and_1_out, not_1_out, not_2_out, Borrowin);
  and and_2 (and_2_out, not_3_out, B, not_4_out);
  and and_3 (and_3_out, A, not_5_out, not_6_out);
  and and_4 (and_4_out, A, B, Borrowin);
  and and_5 (and_5_out, not_7_out, Borrowin);
  and and_6 (and_6_out, not_8_out, B);
  and and_7 (and_7_out, B, Borrowin);
  or or_1 (\Subtração , and_1_out, and_2_out, and_3_out, and_4_out);
  or or_2 (Borrowout, and_5_out, and_6_out, and_7_out);
endmodule

module Subtracao_8bit (
  input  A7,
  input  A6,
  input  A5,
  input  A4,
  input  A3,
  input  A2,
  input  A1,
  input  A0,
  input  B7,
  input  B6,
  input  B5,
  input  B4,
  input  B3,
  input  B2,
  input  B1,
  input  B0,
  output out_17,
  output S7,
  output S6,
  output S5,
  output S4,
  output S3,
  output S2,
  output S1,
  output S0
);

  wire subtracao_2_borrowout, subtracao_3_borrowout, subtracao_4_borrowout, subtracao_5_borrowout,
       subtracao_6_borrowout, subtracao_7_borrowout, subtracao_8_borrowout;

  Subtracao subtracao_1 (.B(B7), .A(A7), .Borrowin(subtracao_2_borrowout), .\Subtração (S7), .Borrowout(out_17));
  Subtracao subtracao_2 (
    .B(B6), .A(A6), .Borrowin(subtracao_4_borrowout), .\Subtração (S6), .Borrowout(subtracao_2_borrowout));
  Subtracao subtracao_3 (
    .B(B4), .A(A4), .Borrowin(subtracao_5_borrowout), .\Subtração (S4), .Borrowout(subtracao_3_borrowout));
  Subtracao subtracao_4 (
    .B(B5), .A(A5), .Borrowin(subtracao_3_borrowout), .\Subtração (S5), .Borrowout(subtracao_4_borrowout));
  Subtracao subtracao_5 (
    .B(B3), .A(A3), .Borrowin(subtracao_6_borrowout), .\Subtração (S3), .Borrowout(subtracao_5_borrowout));
  Subtracao subtracao_6 (
    .B(B2), .A(A2), .Borrowin(subtracao_7_borrowout), .\Subtração (S2), .Borrowout(subtracao_6_borrowout));
  Subtracao subtracao_7 (
    .B(B1), .A(A1), .Borrowin(subtracao_8_borrowout), .\Subtração (S1), .Borrowout(subtracao_7_borrowout));
  Subtracao subtracao_8 (.B(B0), .A(A0), .Borrowin(1'b0), .\Subtração (S0), .Borrowout(subtracao_8_borrowout));

  // Notes on the sheet:
  //   A
endmodule

module OR (
  input  A0,
  input  A1,
  input  A2,
  input  A3,
  input  A4,
  input  A5,
  input  A6,
  input  A7,
  input  B0,
  input  B1,
  input  B2,
  input  B3,
  input  B4,
  input  B5,
  input  B6,
  input  B7,
  output OR
);

  or or_1 (OR, A0, A1, A2, A3, A4, A5, A6, A7, B0, B1, B2, B3, B4, B5, B6, B7);
endmodule

module AND (
  input  A0,
  input  A1,
  input  A2,
  input  A3,
  input  A4,
  input  A5,
  input  A6,
  input  A7,
  input  B0,
  input  B1,
  input  B2,
  input  B3,
  input  B4,
  input  B5,
  input  B6,
  input  B7,
  output AND
);

  and and_1 (AND, A0, A1, A2, A3, A4, A5, A6, A7, B0, B1, B2, B3, B4, B5, B6, B7);
endmodule

module Maior_8bit (
  input  A0,
  input  A1,
  input  A2,
  input  A3,
  input  A4,
  input  A5,
  input  A6,
  input  A7,
  input  B0,
  input  B1,
  input  B2,
  input  B3,
  input  B4,
  input  B5,
  input  B6,
  input  B7,
  output out_17
);

  wire and_1_out, and_2_out, and_3_out, and_4_out, and_5_out, and_6_out, and_7_out, and_8_out, and_9_out,
       and_10_out, and_11_out, and_12_out, and_13_out, and_14_out, and_15_out, and_16_out, and_18_out,
       and_19_out, and_20_out, and_21_out, and_22_out, and_23_out, and_24_out, nor_1_out, nor_2_out,
       nor_4_out, nor_5_out, nor_7_out, nor_8_out, not_1_out, not_2_out, not_3_out, not_4_out, not_5_out,
       not_6_out, not_7_out, not_8_out, not_9_out, not_10_out, not_11_out, not_12_out, not_13_out,
       not_14_out, not_15_out, not_16_out;

  not not_1 (not_1_out, A0);
  not not_2 (not_2_out, B0);
  not not_3 (not_3_out, A1);
  not not_4 (not_4_out, B1);
  not not_5 (not_5_out, A2);
  not not_6 (not_6_out, B2);
  not not_7 (not_7_out, A3);
  not not_8 (not_8_out, B3);
  not not_9 (not_9_out, A4);
  not not_10 (not_10_out, B4);
  not not_11 (not_11_out, A5);
  not not_12 (not_12_out, B5);
  not not_13 (not_13_out, A6);
  not not_14 (not_14_out, B6);
  not not_15 (not_15_out, A7);
  not not_16 (not_16_out, B7);
  and and_1 (and_1_out, not_1_out, B0);
  and and_2 (and_2_out, A0, not_2_out);
  and and_3 (and_3_out, not_3_out, B1);
  and and_4 (and_4_out, A1, not_4_out);
  and and_5 (and_5_out, not_5_out, B2);
  and and_6 (and_6_out, A2, not_6_out);
  and and_7 (and_7_out, not_7_out, B3);
  and and_8 (and_8_out, A3, not_8_out);
  and and_9 (and_9_out, not_9_out, B4);
  and and_10 (and_10_out, A4, not_10_out);
  and and_11 (and_11_out, not_11_out, B5);
  and and_12 (and_12_out, A5, not_12_out);
  and and_13 (and_13_out, not_13_out, B6);
  and and_14 (and_14_out, A6, not_14_out);
  and and_15 (and_15_out, not_15_out, B7);
  and and_16 (and_16_out, A7, not_16_out);
  nor nor_1 (nor_1_out, and_1_out, and_2_out);
  nor nor_2 (nor_2_out, and_3_out, and_4_out);
  // NOR_Gate nor_3 has open pins: in0=and_5_out, in1=and_6_out, out=open
  nor nor_4 (nor_4_out, and_7_out, and_8_out);
  nor nor_5 (nor_5_out, and_9_out, and_10_out);
  nor nor_6 (nor_5_out, and_11_out, and_12_out);
  nor nor_7 (nor_7_out, and_13_out, and_14_out);
  nor nor_8 (nor_8_out, and_15_out, and_16_out);
  // AND_Gate and_17 has open pins: in0=nor_1_out, in1=and_3_out, out=open
  and and_18 (and_18_out, nor_1_out, and_4_out);
  and and_19 (and_19_out, nor_1_out, nor_2_out, and_6_out);
  and and_20 (and_20_out, nor_1_out, nor_2_out, nor_4_out, and_8_out);
  and and_21 (and_21_out, nor_1_out, nor_2_out, nor_4_out, nor_5_out, and_10_out);
  and and_22 (and_22_out, nor_1_out, nor_2_out, nor_4_out, nor_5_out, nor_5_out, and_12_out);
  and and_23 (and_23_out, nor_1_out, nor_2_out, nor_4_out, nor_5_out, nor_5_out, nor_7_out, and_14_out);
  and and_24 (and_24_out, nor_1_out, nor_2_out, nor_4_out, nor_5_out, nor_5_out, nor_7_out, nor_8_out, and_16_out);
  or or_1 (out_17, and_2_out, and_18_out, and_19_out, and_20_out, and_21_out, and_22_out, and_23_out, and_24_out);

  // Notes on the sheet:
  //   A maior que B
endmodule

module Igual (
  input  A,
  input  B,
  output Igual
);

  wire and_1_out, and_2_out, not_1_out, not_2_out;

  not not_1 (not_1_out, A);
  not not_2 (not_2_out, B);
  and and_1 (and_1_out, not_1_out, not_2_out);
  buf and_2 (and_2_out, A);  // AND_Gate
  or or_1 (Igual, and_1_out, and_2_out);
endmodule

module Igual_8bit (
  input  A0,
  input  A1,
  input  A2,
  input  A3,
  input  A4,
  input  A5,
  input  A6,
  input  A7,
  input  B0,
  input  B1,
  input  B2,
  input  B3,
  input  B4,
  input  B5,
  input  B6,
  input  B7,
  output Igual
);

  wire igual_1_igual, igual_2_igual, igual_3_igual, igual_4_igual, igual_5_igual, igual_6_igual,
       igual_7_igual, igual_8_igual;

  Igual igual_1 (.A(A0), .B(B0), .Igual(igual_1_igual));
  Igual igual_2 (.A(A1), .B(B1), .Igual(igual_2_igual));
  Igual igual_3 (.A(A2), .B(B2), .Igual(igual_3_igual));
  Igual igual_4 (.A(A3), .B(B3), .Igual(igual_4_igual));
  Igual igual_5 (.A(A4), .B(B4), .Igual(igual_5_igual));
  Igual igual_6 (.A(A5), .B(B5), .Igual(igual_6_igual));
  Igual igual_7 (.A(A6), .B(B6), .Igual(igual_7_igual));
  Igual igual_8 (.A(A7), .B(B7), .Igual(igual_8_igual));
  and and_1 (Igual, igual_1_igual, igual_2_igual, igual_3_igual, igual_4_igual, igual_5_igual, igual_6_igual, igual_7_igual, igual_8_igual);
endmodule

module Menor_8bit (
  input  A0,
  input  A1,
  input  A2,
  input  A3,
  input  A4,
  input  A5,
  input  A6,
  input  A7,
  input  B0,
  input  B1,
  input  B2,
  input  B3,
  input  B4,
  input  B5,
  input  B6,
  input  B7,
  output out_17
);

  wire and_1_out, and_2_out, and_3_out, and_4_out, and_5_out, and_6_out, and_7_out, and_8_out, and_9_out,
       and_10_out, and_11_out, and_12_out, and_13_out, and_14_out, and_15_out, and_16_out, and_17_out,
       and_18_out, and_19_out, and_20_out, and_21_out, and_22_out, and_23_out, nor_1_out, nor_2_out,
       nor_3_out, nor_4_out, nor_5_out, nor_6_out, nor_7_out, not_1_out, not_2_out, not_3_out, not_4_out,
       not_5_out, not_6_out, not_7_out, not_8_out, not_9_out, not_10_out, not_11_out, not_12_out, not_13_out,
       not_14_out, not_15_out, not_16_out;

  not not_1 (not_1_out, A0);
  not not_2 (not_2_out, B0);
  not not_3 (not_3_out, A1);
  not not_4 (not_4_out, B1);
  not not_5 (not_5_out, A2);
  not not_6 (not_6_out, B2);
  not not_7 (not_7_out, A3);
  not not_8 (not_8_out, B3);
  not not_9 (not_9_out, A4);
  not not_10 (not_10_out, B4);
  not not_11 (not_11_out, A5);
  not not_12 (not_12_out, B5);
  not not_13 (not_13_out, A6);
  not not_14 (not_14_out, B6);
  not not_15 (not_15_out, A7);
  not not_16 (not_16_out, B7);
  and and_1 (and_1_out, not_1_out, B0);
  and and_2 (and_2_out, A0, not_2_out);
  and and_3 (and_3_out, not_3_out, B1);
  and and_4 (and_4_out, A1, not_4_out);
  and and_5 (and_5_out, not_5_out, B2);
  and and_6 (and_6_out, A2, not_6_out);
  and and_7 (and_7_out, not_7_out, B3);
  and and_8 (and_8_out, A3, not_8_out);
  and and_9 (and_9_out, not_9_out, B4);
  and and_10 (and_10_out, A4, not_10_out);
  and and_11 (and_11_out, not_11_out, B5);
  and and_12 (and_12_out, A5, not_12_out);
  and and_13 (and_13_out, not_13_out, B6);
  and and_14 (and_14_out, A6, not_14_out);
  and and_15 (and_15_out, not_15_out, B7);
  and and_16 (and_16_out, A7, not_16_out);
  nor nor_1 (nor_1_out, and_1_out, and_2_out);
  nor nor_2 (nor_2_out, and_3_out, and_4_out);
  nor nor_3 (nor_3_out, and_5_out, and_6_out);
  nor nor_4 (nor_4_out, and_7_out, and_8_out);
  nor nor_5 (nor_5_out, and_9_out, and_10_out);
  nor nor_6 (nor_6_out, and_11_out, and_12_out);
  nor nor_7 (nor_7_out, and_13_out, and_14_out);
  // NOR_Gate nor_8 has open pins: in0=and_15_out, in1=and_16_out, out=open
  and and_17 (and_17_out, nor_1_out, and_3_out);
  and and_18 (and_18_out, nor_1_out, and_5_out, nor_2_out);
  and and_19 (and_19_out, nor_1_out, nor_2_out, nor_3_out, and_7_out);
  and and_20 (and_20_out, nor_1_out, nor_2_out, nor_3_out, nor_4_out, and_9_out);
  and and_21 (and_21_out, nor_1_out, nor_2_out, nor_3_out, nor_4_out, nor_5_out, and_11_out);
  and and_22 (and_22_out, nor_1_out, nor_2_out, nor_3_out, nor_4_out, nor_5_out, nor_6_out, and_13_out);
  and and_23 (and_23_out, nor_1_out, nor_2_out, nor_3_out, nor_4_out, nor_5_out, nor_6_out, nor_7_out, and_16_out);
  or or_1 (out_17, and_1_out, and_17_out, and_18_out, and_19_out, and_20_out, and_21_out, and_22_out, and_23_out);

  // Notes on the sheet:
  //   A menor que B
endmodule

module Selecao (
  input  A0,
  input  A1,
  input  A2,
  input  A3,
  input  A4,
  input  A5,
  input  A6,
  input  A7,
  input  B0,
  input  B1,
  input  B2,
  input  B3,
  input  B4,
  input  B5,
  input  B6,
  input  B7,
  input  [2:0] in_17,
  output Carryout,
  output Borrowout,
  output S0,
  output S1,
  output S2,
  output S3,
  output S4,
  output S5,
  output S6,
  output S7
);

  wire and_1_and, igual_8bit_1_igual, maior_8bit_1_out_17, menor_8bit_1_out_17, or_1_or;
  wire [7:0] bit_extender_1_out, bit_extender_2_out, bit_extender_3_out, bit_extender_4_out,
       bit_extender_5_out, soma_8bit_1_out_25, subtracao_8bit_1_s0;

  Soma_8bit soma_8bit_1 (
    .Carry_out(Carryout), .B7(B7), .B6(B6), .B5(B5), .B4(B4), .B3(B3), .B2(B2), .B1(B1), .B0(B0), .A7(A7),
    .A6(A6), .A5(A5), .A4(A4), .A3(A3), .A2(A2), .A1(A1), .A0(A0), .out_18(soma_8bit_1_out_25[7]),
    .out_19(soma_8bit_1_out_25[6]), .out_20(soma_8bit_1_out_25[5]), .out_21(soma_8bit_1_out_25[4]),
    .out_22(soma_8bit_1_out_25[3]), .out_23(soma_8bit_1_out_25[2]), .out_24(soma_8bit_1_out_25[1]),
    .out_25(soma_8bit_1_out_25[0]));
  Subtracao_8bit subtracao_8bit_1 (
    .out_17(Borrowout), .A7(A7), .A6(A6), .A5(A5), .A4(A4), .A3(A3), .A2(A2), .A1(A1), .A0(A0), .B7(B7),
    .B6(B6), .B5(B5), .B4(B4), .B3(B3), .B2(B2), .B1(B1), .B0(B0), .S7(subtracao_8bit_1_s0[7]),
    .S6(subtracao_8bit_1_s0[6]), .S5(subtracao_8bit_1_s0[5]), .S4(subtracao_8bit_1_s0[4]),
    .S3(subtracao_8bit_1_s0[3]), .S2(subtracao_8bit_1_s0[2]), .S1(subtracao_8bit_1_s0[1]),
    .S0(subtracao_8bit_1_s0[0]));
  Igual_8bit igual_8bit_1 (
    .A0(A0), .A1(A1), .A2(A2), .A3(A3), .A4(A4), .A5(A5), .A6(A6), .A7(A7), .B0(B0), .B1(B1), .B2(B2),
    .B3(B3), .B4(B4), .B5(B5), .B6(B6), .B7(B7), .Igual(igual_8bit_1_igual));
  OR or_1 (
    .A0(A0), .A1(A1), .A2(A2), .A3(A3), .A4(A4), .A5(A5), .A6(A6), .A7(A7), .B0(B0), .B1(B1), .B2(B2),
    .B3(B3), .B4(B4), .B5(B5), .B6(B6), .B7(B7), .OR(or_1_or));
  AND and_1 (
    .A0(A0), .A1(A1), .A2(A2), .A3(A3), .A4(A4), .A5(A5), .A6(A6), .A7(A7), .B0(B0), .B1(B1), .B2(B2),
    .B3(B3), .B4(B4), .B5(B5), .B6(B6), .B7(B7), .AND(and_1_and));
  Maior_8bit maior_8bit_1 (
    .A0(A0), .A1(A1), .A2(A2), .A3(A3), .A4(A4), .A5(A5), .A6(A6), .A7(A7), .B0(B0), .B1(B1), .B2(B2),
    .B3(B3), .B4(B4), .B5(B5), .B6(B6), .B7(B7), .out_17(maior_8bit_1_out_17));
  Menor_8bit menor_8bit_1 (
    .A0(A0), .A1(A1), .A2(A2), .A3(A3), .A4(A4), .A5(A5), .A6(A6), .A7(A7), .B0(B0), .B1(B1), .B2(B2),
    .B3(B3), .B4(B4), .B5(B5), .B6(B6), .B7(B7), .out_17(menor_8bit_1_out_17));
  assign bit_extender_1_out = {{7{1'b0}}, igual_8bit_1_igual};  // Bit_Extender bit_extender_1
  assign bit_extender_2_out = {{7{1'b0}}, or_1_or};  // Bit_Extender bit_extender_2
  assign bit_extender_3_out = {{7{1'b0}}, and_1_and};  // Bit_Extender bit_extender_3
  assign bit_extender_4_out = {{7{1'b0}}, maior_8bit_1_out_17};  // Bit_Extender bit_extender_4
  assign bit_extender_5_out = {{7{1'b0}}, menor_8bit_1_out_17};  // Bit_Extender bit_extender_5
  Multiplexer #(.select(3), .width(8)) multiplexer_1 (
    .in0(soma_8bit_1_out_25), .in1(subtracao_8bit_1_s0), .in2(bit_extender_1_out), .in3(bit_extender_2_out),
    .in4(bit_extender_3_out), .in5(bit_extender_4_out), .in6(bit_extender_5_out),
    .out({S7, S6, S5, S4, S3, S2, S1, S0}), .sel(in_17), .en(1'b1));  // open: in7
endmodule

module \Comparação  (
  input  A0,
  input  A1,
  input  A2,
  input  A3,
  input  A4,
  input  A5,
  input  A6,
  input  A7,
  input  A_B,
  input  A_B_2,
  input  B0,
  input  B1,
  input  Negativo,
  input  B2,
  input  B3,
  input  B4,
  input  B5,
  input  B6,
  input  B7,
  output A_B_3
);

  Comparator comparator_1 (
    .a({A7, A6, A5, A4, A3, A2, A1, A0}), .b({B7, B6, B5, B4, B3, B2, B1, B0}), .gt(A_B_3), .eq(A_B),
    .lt(A_B_2));

  assign Negativo = A_B_2;
endmodule

module Hexa_7segmentos (
  input  a,
  input  b,
  input  c,
  input  d
);

  wire not_1_out, not_2_out, not_3_out, not_4_out, not_5_out, not_6_out, not_7_out, not_8_out, not_9_out,
       not_10_out, not_11_out, not_12_out;

  not not_1 (not_1_out, b);
  not not_2 (not_2_out, d);
  not not_3 (not_3_out, a);
  not not_4 (not_4_out, a);
  not not_5 (not_5_out, b);
  not not_6 (not_6_out, c);
  not not_7 (not_7_out, d);
  not not_8 (not_8_out, a);
  not not_9 (not_9_out, b);
  not not_10 (not_10_out, a);
  not not_11 (not_11_out, c);
  not not_12 (not_12_out, d);
  // AND_Gate and_1 has open pins: in0=not_1_out, in1=not_2_out, out=open
  // AND_Gate and_2 has open pins: in0=not_3_out, in1=c, out=open
  // AND_Gate and_3 has open pins: in0=not_4_out, in1=b, in2=d, out=open
  // AND_Gate and_4 has open pins: in0=b, in1=c, out=open
  // AND_Gate and_5 has open pins: in0=a, in1=not_5_out, in2=not_6_out, out=open
  // AND_Gate and_6 has open pins: in0=a, in1=not_7_out, out=open
  // AND_Gate and_7 has open pins: in0=not_8_out, in1=not_9_out, out=open
  // AND_Gate and_8 has open pins: in0=not_10_out, in1=not_11_out, in2=not_12_out, out=open
  // AND_Gate and_9 is placed but not wired
  // AND_Gate and_10 is placed but not wired
  // AND_Gate and_11 is placed but not wired
  // AND_Gate and_12 is placed but not wired
  // AND_Gate and_13 is placed but not wired
  // AND_Gate and_14 is placed but not wired
  // AND_Gate and_15 is placed but not wired
  // AND_Gate and_16 is placed but not wired
  // AND_Gate and_17 is placed but not wired
  // AND_Gate and_18 is placed but not wired
  // AND_Gate and_19 is placed but not wired
  // AND_Gate and_20 is placed but not wired
  // AND_Gate and_21 is placed but not wired
  // AND_Gate and_22 is placed but not wired
endmodule

module \Operações  (
  input  A0,
  input  A1,
  input  A2,
  input  A3,
  input  A4,
  input  A5,
  input  A6,
  input  A7,
  input  B0,
  input  B1,
  input  B2,
  input  B3,
  input  B4,
  input  B5,
  input  [2:0] in_15,
  input  B6,
  input  B7,
  output Carryin,
  output Borrowout,
  output S0,
  output S1,
  output S2,
  output S3,
  output S4,
  output S5,
  output S6,
  output S7,
  output A___B,
  output A___B_2,
  output A___B_3,
  output Negativo
);

  Selecao selecao_1 (
    .A0(A0), .A1(A1), .A2(A2), .A3(A3), .A4(A4), .A5(A5), .A6(A6), .A7(A7), .B0(B0), .B1(B1), .B2(B2),
    .B3(B3), .B4(B4), .B5(B5), .B6(B6), .B7(B7), .in_17({in_15[2:1], B7}), .Borrowout(Borrowout),
    .Carryout(Carryin), .S0(S0), .S1(S1), .S2(S2), .S3(S3), .S4(S4), .S5(S5), .S6(S6), .S7(S7));
  \Comparação  \comparação_1  (
    .A0(A0), .A1(A1), .A2(A2), .A3(A3), .A4(A4), .A5(A5), .A6(A6), .A7(A7), .B0(B0), .B1(B1), .B2(B3),
    .B3(B4), .B4(B5), .B5(B6), .B6(B7), .A_B_3(A___B), .A_B(A___B_2), .A_B_2(A___B_3), .Negativo(Negativo));  // open: B7
  // Pins of 1 and 3 bits meet at {in_15[2:1], B7}

  assign in_15[0] = B7;
endmodule
